# Fritzing sketch Radar (saved by Fritzing 1.0.6)
breadboards: 1

parts:
  Part1 = Arduino Uno (Rev3)
  J3 = Infrared Proximity Sensor [distance_to_obstacle=50%]
  J4 = Basic Servo
  LCD1 = 2.8" SPI TFT Module [part_number=MSP2807]
  LLC1 = Logic Level Converter [package="Breakout board"]
  LLC2 = Logic Level Converter [package="Breakout board"]

nets:
  N1: Part1.A0, J3.Vout
  N2: Part1.D8, LLC1.HV2
  N3: Part1.D9_PWM, LLC1.HV1
  N4: Part1.D10_PWM/SS, LLC1.HV3
  N5: Part1.D11_PWM/MOSI, LLC2.HV1
  N6: Part1.D13/SCK, LLC2.HV3
  GND: Part1.GND, J3.GND, J4.gnd, LLC1.H-GND, LLC2.H-GND
  N7: Part1.D5_PWM, J4.pulse
  N8: Part1.3V3, LLC1.LV, LLC2.LV
  VCC: Part1.5V, J3.Vcc, J4.vcc, LCD1.pin1, LCD1.pin8, LLC1.HV, LLC2.HV
  N9: LCD1.pin2, LLC1.L-GND, LLC2.L-GND
  N10: LCD1.pin3, LLC1.LV2
  N11: LCD1.pin4, LLC1.LV1
  N12: LCD1.pin5, LLC1.LV3
  N13: LCD1.pin6, LLC2.LV1
  N14: LCD1.pin7, LLC2.LV3

custom parts:
  2.8" SPI TFT Module: A generic 2.8 inch LCD TFT 320x240 display with touchscreen and SD card slot. Uses the ILI9341 controller, like the Adafruit displays of this size uses.
  Logic Level Converter: 5V to/from 3.3V logic level converter
